// Logisim project CC84.circ as structural Verilog: 6 circuits, main circuit main
module main (
);

  wire alu_1_v, clk, decoder_1_out1, decoder_1_out2, decoder_1_out3, decoder_1_out4, decoder_1_out5,
       decoder_1_out8, dipswitch_1_sw7, dipswitch_1_sw8, R;
  wire [1:0] decoder_1_out6;
  wire [3:0] cu_1_add, cu_1_ins, register_1_q, register_2_q;
  wire [7:0] alu_1_y, pc_1_clock_value, pc_1_op, ram_1_data, register_3_q, register_4_q;

  Clock clock_1 (.out(clk));
  Register #(.width(4)) register_1 (.D(cu_1_add), .en(decoder_1_out4), .clk(clk), .Q(register_1_q), .clr(R));
  RAM #(.addrWidth(4), .databus("bidir")) ram_1 (
    .addr(register_1_q), .we(decoder_1_out6[0]), .oe(decoder_1_out6[1]), .clk(clk), .data(ram_1_data));
  Decoder #(.enable("false"), .select(4)) decoder_1 (
    .out1(decoder_1_out1), .out2(decoder_1_out2), .out3(decoder_1_out3), .out4(decoder_1_out4),
    .out5(decoder_1_out5), .out6(decoder_1_out6[0]), .out7(decoder_1_out6[1]), .out8(decoder_1_out8),
    .out15(R), .sel(cu_1_ins));  // open: out0, out9, out10, out11, out12, out13, out14
  CU cu_1 (.INS_IN(pc_1_op[3:0]), .ADD_IN(pc_1_op[7:4]), .ADD(cu_1_add), .INS(cu_1_ins));
  // LedBar #(.inputtype("row")) ledbar_1: pin names not known; wires that end beside it: ram_1_data[5], ram_1_data[4], ram_1_data[3], ram_1_data[2], ram_1_data[1], ram_1_data[0], ram_1_data
  Register #(.width(4)) register_2 (.D(ram_1_data[3:0]), .en(decoder_1_out3), .clk(clk), .Q(register_2_q), .clr(R));
  Register register_3 (.D(ram_1_data), .en(decoder_1_out1), .clk(clk), .Q(register_3_q), .clr(R));
  Register register_4 (.D(ram_1_data), .en(decoder_1_out2), .clk(clk), .Q(register_4_q), .clr(R));
  PC pc_1 (
    .JMP(decoder_1_out8), .JMP_VALUE(ram_1_data), .START(dipswitch_1_sw8), .CLK(clk),
    .RESET(dipswitch_1_sw7), .CLOCK_VALUE(pc_1_clock_value), .OP(pc_1_op), .DATA(ram_1_data));
  DipSwitch dipswitch_1 (.sw7(dipswitch_1_sw7), .sw8(dipswitch_1_sw8));  // open: sw1, sw2, sw3, sw4, sw5, sw6
  ALU alu_1 (.A(register_3_q), .B(register_4_q), .UPCODE(register_2_q), .V(alu_1_v), .Y(alu_1_y));  // open: Z, N, C
  Register register_5 (.D(alu_1_y), .en(decoder_1_out5), .clk(clk), .clr(R));  // open: Q
  LedBar ledbar_2 (
    .led0(alu_1_y[7]), .led1(alu_1_y[6]), .led2(alu_1_y[5]), .led3(alu_1_y[4]), .led4(alu_1_y[3]),
    .led5(alu_1_y[2]), .led6(alu_1_y[1]), .led7(alu_1_y[0]));
  Hex_Digit_Display hex_digit_display_1 (.value(pc_1_clock_value[7:4]));  // open: dp
  Hex_Digit_Display hex_digit_display_2 (.value(pc_1_clock_value[3:0]));  // open: dp
  LED OVERFLOW (.in(alu_1_v));
  Hex_Digit_Display hex_digit_display_3 (.value(alu_1_y[7:4]));  // open: dp
  Hex_Digit_Display hex_digit_display_4 (.value(alu_1_y[3:0]));  // open: dp
  _7_Segment_Display u_7_segment_display_1 ();  // open: g, f, a, b, e, d, c, dp
  // BCD_to_7_Segment_decoder bcd_to_7_segment_decoder_1: pin names not known
  Bit_Extender #(.out_width(9)) bit_extender_1 (.in(pc_1_clock_value));  // open: out
  // Binary_to_BCD_converter binary_to_bcd_converter_1: pin names not known
  _7_Segment_Display u_7_segment_display_2 ();  // open: g, f, a, b, e, d, c, dp
  // BCD_to_7_Segment_decoder bcd_to_7_segment_decoder_2: pin names not known
  Bit_Extender #(.out_width(9)) bit_extender_2 (.in(alu_1_y));  // open: out
  // Binary_to_BCD_converter binary_to_bcd_converter_2: pin names not known
  _7_Segment_Display u_7_segment_display_3 ();  // open: g, f, a, b, e, d, c, dp
  // BCD_to_7_Segment_decoder bcd_to_7_segment_decoder_3: pin names not known
  _7_Segment_Display u_7_segment_display_4 ();  // open: g, f, a, b, e, d, c, dp
  // BCD_to_7_Segment_decoder bcd_to_7_segment_decoder_4: pin names not known
  _7_Segment_Display u_7_segment_display_5 ();  // open: g, f, a, b, e, d, c, dp
  // BCD_to_7_Segment_decoder bcd_to_7_segment_decoder_5: pin names not known
  _7_Segment_Display u_7_segment_display_6 ();  // open: g, f, a, b, e, d, c, dp
  // BCD_to_7_Segment_decoder bcd_to_7_segment_decoder_6: pin names not known

  // Notes on the sheet:
  //   ADDRES_BUS
  //   3210
  //   MAR
  //   DATA_BUS
  //   76543210
  //   A REG
  //   B REG
  //   Control_Panel
  //   OUTPUT REG
  //   End value
endmodule

module ALU (
  input  [7:0] A,
  input  [7:0] B,
  input  [3:0] UPCODE,
  output Z,
  output V,
  output N,
  output C,
  output [7:0] Y
);

  wire [7:0] au_1_y, lu_1_y, multiplexer_1_out, multiplexer_2_out, not_1_out, not_2_out;

  assign not_1_out = ~A;  // NOT_Gate not_1, 8 bits wide
  assign not_2_out = ~B;  // NOT_Gate not_2, 8 bits wide
  Multiplexer #(.width(8)) multiplexer_1 (.in0(A), .in1(not_1_out), .out(multiplexer_1_out), .sel(UPCODE[0]));
  Multiplexer #(.width(8)) multiplexer_2 (.in0(B), .in1(not_2_out), .out(multiplexer_2_out), .sel(UPCODE[1]));
  AU au_1 (.CIN(UPCODE[2]), .A(multiplexer_1_out), .B(multiplexer_2_out), .Y(au_1_y), .OVERFLOW(V), .COUT(C));
  LU lu_1 (.A(A), .B(multiplexer_2_out), .F2(UPCODE[2]), .F0(UPCODE[0]), .Y(lu_1_y));
  Multiplexer #(.width(8)) multiplexer_3 (.in0(au_1_y), .in1(lu_1_y), .out({N, Y[6:0]}), .sel(UPCODE[3]));
  nor nor_1 (Z, Y[0], Y[1], Y[2], Y[3], Y[4], Y[5], Y[6], N);

  assign Y[7] = N;
endmodule

module AU (
  input  CIN,
  input  [7:0] A,
  input  [7:0] B,
  output [7:0] Y,
  output OVERFLOW,
  output COUT
);

  wire adder_1_cout, adder_2_cout, adder_3_cout, adder_4_cout, adder_5_cout, adder_6_cout, adder_7_cout;

  Adder #(.width(1)) adder_1 (.a(A[0]), .b(B[0]), .out(Y[0]), .cin(CIN), .cout(adder_1_cout));
  Adder #(.width(1)) adder_2 (.a(A[1]), .b(B[1]), .out(Y[1]), .cin(adder_1_cout), .cout(adder_2_cout));
  Adder #(.width(1)) adder_3 (.a(A[2]), .b(B[2]), .out(Y[2]), .cin(adder_2_cout), .cout(adder_3_cout));
  Adder #(.width(1)) adder_4 (.a(A[3]), .b(B[3]), .out(Y[3]), .cin(adder_3_cout), .cout(adder_4_cout));
  Adder #(.width(1)) adder_5 (.a(A[4]), .b(B[4]), .out(Y[4]), .cin(adder_4_cout), .cout(adder_5_cout));
  Adder #(.width(1)) adder_6 (.a(A[5]), .b(B[5]), .out(Y[5]), .cin(adder_5_cout), .cout(adder_6_cout));
  Adder #(.width(1)) adder_7 (.a(A[6]), .b(B[6]), .out(Y[6]), .cin(adder_6_cout), .cout(adder_7_cout));
  Adder #(.width(1)) adder_8 (.a(A[7]), .b(B[7]), .out(Y[7]), .cin(adder_7_cout), .cout(COUT));
  xor xor_1 (OVERFLOW, adder_7_cout, COUT);
endmodule

module LU (
  input  [7:0] A,
  input  [7:0] B,
  input  F2,
  input  F0,
  output [7:0] Y
);

  wire [7:0] and_1_out, or_1_out, xor_1_out;

  assign and_1_out = A & B;  // AND_Gate and_1, 8 bits wide
  assign or_1_out = A | B;  // OR_Gate or_1, 8 bits wide
  assign xor_1_out = A ^ B;  // XOR_Gate xor_1, 8 bits wide
  Multiplexer #(.select(2), .width(8)) multiplexer_1 (
    .in0(and_1_out), .in1(or_1_out), .in2(xor_1_out), .in3(B), .out(Y), .sel({F2, F0}));
endmodule

module CU (
  input  [3:0] INS_IN,
  input  [3:0] ADD_IN,
  output [3:0] ADD,
  output [3:0] INS
);

  ROM #(.addrWidth(4), .dataWidth(4)) rom_1 (.addr(ADD_IN), .data(ADD));
  ROM #(.addrWidth(4), .dataWidth(4)) rom_2 (.addr(INS_IN), .data(INS));

  // Notes on the sheet:
  //   contents of rom_1 (hex, n*v repeats v):
  //   0 1 2 3 4 5 6 7 8 9 a b c d e f
  //   contents of rom_2 (hex, n*v repeats v):
  //   0 1 2 3 4 5 6 7 8 9 a b c d e f
  //   MEMORY_ADDRES
  //   INSTRUCTION
endmodule

module PC (
  input  JMP,
  input  [7:0] JMP_VALUE,
  input  START,
  input  CLK,
  input  RESET,
  output [7:0] CLOCK_VALUE,
  output [7:0] OP,
  output [7:0] DATA
);

  Counter counter_1 (
    .load(JMP), .D(JMP_VALUE), .count(START), .Q(CLOCK_VALUE), .clk(CLK), .clr(RESET));  // open: carry, up
  ROM #(.dataWidth(16)) rom_1 (.addr(CLOCK_VALUE), .data({DATA, OP}));

  // Notes on the sheet:
  //   contents of rom_1 (hex, n*v repeats v):
  //   2701 1e02 5
endmodule
